# Fritzing sketch Wiring_diagram (saved by Fritzing 0.9.10b)
breadboards: 1
perfboards: 1

parts:
  Mic = INMP441
  16x16_led_matrix = WS2812 RGB LED matrix 8x8
  Mode_selection = Pushbutton [package="[THT]"]
  S1 = Toggle Switch [package=THT]
  Mic_gain = Rotary Potentiometer (Small) [maximum_resistance=100kΩ knob_status=50% power=0.5W package=THT]
  Mic_threshold = Rotary Potentiometer (Small) [maximum_resistance=100kΩ knob_status=50% power=0.5W package=THT]
  Brightness = Rotary Potentiometer (Small) [maximum_resistance=100kΩ knob_status=50% power=0.5W package=THT]
  A1 = ESP32 DevKitc V4
  C1 = Electrolytic Capacitor [capacitance=100µF voltage=25V package="100 mil [THT, electrolytic]"]
  C2 = Ceramic Capacitor [capacitance=63nF voltage=25V package="100 mil [THT, multilayer]"]

nets:
  GND: Mic.L/R, Mic.GND, 16x16_led_matrix.GND, Mode_selection.Pin_1, Mic_gain.leg2, Mic_threshold.leg2, Brightness.leg2, A1.Pin_14, A1.Pin_32, A1.Pin_38, C1.-, C2.0
  N1: Mic.WS, A1.Pin_23
  N2: Mic.SCK, A1.Pin_12
  N3: Mic.SD, A1.Pin_7
  N4: Mic.VDD, Mic_gain.leg1, Mic_threshold.leg1, Brightness.leg1, A1.Pin_1
  N5: 16x16_led_matrix.VCC, S1.COM, A1.Pin_19, C1.+, C2.1
  N6: 16x16_led_matrix.DIN, A1.Pin_36
  N7: Mode_selection.Pin_3, Mode_selection.Pin_4, A1.Pin_33
  5V: S1.L2
  N8: Mic_gain.wiper, A1.Pin_8
  N9: Mic_threshold.wiper, A1.Pin_5
  N10: Brightness.wiper, A1.Pin_6

custom parts:
  INMP441: This is a simple breakout board for the INMP441 I2S MEMS microphone.
  WS2812 RGB LED matrix 8x8: WS2812 matrix 8x8
  ESP32 DevKitc V4: ESP32-DevKitC board with ESP32-WROOM-32 module. ESP32-DevKitC V4 is a small-sized ESP32-based development board produced by Espressif. Most of the pins on the ESP module are broken out to the pin headers on the board. The pins D0, D1, D2, D3, CMD and CLK are used internally for communication between ESP32 and SPI flash memory. They are grouped on both sides near the USB connector. Avoid using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
